# Fritzing sketch home-automation-model (saved by Fritzing 0.9.3b)
breadboards: 1

parts:
  Raspberry_Pi_1 = Raspberry Pi 3 [part_number=RPI-3-V1.2]  # not connected
  U1 = NodeMCU V1.0
  VCC1 = Battery block 9V
  LED1 = LEDs [package=led10mm]
  U2 = 2-Channel 5v Relay Shield [package=relay-2ch5v10a]

nets:
  N1: U1.D0, U2.IN1
  GND: U1.GND, VCC1.-, U2.GND
  VIN: U1.Vin, VCC1.+, U2.VCC
  N2: LED1.C, U2.K1-On
  N3: LED1.A, U2.K1-In

notes:
  Power supply for the ESP8266 might as well occur through:
  - A USB port
  - A supply regulator connected to a battery
  - A phone charger
  - A 9v battery
  ESP8266 has a tension regulator of 3.3v

custom parts:
  NodeMCU V1.0: ESP8266 based NodeMCU
  2-Channel 5v Relay Shield: 2 Channel 5v Relay Shield w. 2x SPD-06VDC-SD-C
